# Fritzing sketch knock_drop (saved by Fritzing 0.8.5b)
breadboards: 1

parts:
  Bauteil1 = Arduino Uno (Rev3)
  J1 = Piezo Speaker
  J2 = Basic Servo
  LED1 = LED - 5mm [color="White (6500K)" package="5 mm [THT]"]
  R1 = Resistor [tolerance=±5% resistance=220 package=THT]
  R2 = Resistor [tolerance=±5% resistance=1M package=THT]

nets:
  N1: Bauteil1.A0, J1.pin2, R2.Pin_1
  N2: Bauteil1.D9_PWM, J2.pulse
  GND: Bauteil1.GND, J1.pin1, J2.gnd, R1.Pin_0, R2.Pin_0
  N3: Bauteil1.D7, LED1.anode
  5V: Bauteil1.5V, J2.vcc
  N4: LED1.cathode, R1.Pin_1
