# Fritzing sketch musclewire_test1_1 (saved by Fritzing 0.8.5b)
breadboards: 1

parts:
  Bauteil1 = Arduino Uno (Rev3)
  R1 = Resistor [tolerance=±5% resistance=220 package=THT]
  LED1 = LED - 5mm [color="Red (633nm)" package="5 mm [THT]"]
  S1 = Pushbutton [package=THT]

nets:
  N1: Bauteil1.D13/SCK, R1.Pin_1
  N2: Bauteil1.GND, Bauteil1.D2, LED1.cathode, S1.leg0
  N3: Bauteil1.5V, S1.leg1
  N4: R1.Pin_0, LED1.anode

notes:
  Musclewire
