# Fritzing sketch Handpong (saved by Fritzing 0.8.5b)
breadboards: 1

parts:
  Bauteil1 = Arduino Uno (Rev3)
  Q1 = Basic FET N-Channel [package="TO220 [THT]"]
  Q2 = Basic FET N-Channel [package="TO220 [THT]"]
  Power_plug1 = Power plug
  U1 = CAPSENSE_PAD [package=capsense_pad]
  U2 = CAPSENSE_PAD [package=capsense_pad]

nets:
  N1: Bauteil1.D8, U2.RECEIVE
  GND: Bauteil1.GND, Power_plug1.GND
  N2: Bauteil1.D2, U1.RES
  N3: Bauteil1.D5_PWM, Q1.gate
  N4: Bauteil1.5V, U1.RECEIVE, U2.RES
  N5: Q1.source, Q2.source, Power_plug1.VCC
